# Fritzing sketch Gesture Controlled Robot (saved by Fritzing 0.9.3b)
breadboards: 2

parts:
  U1 = L9110 H-bridge module [part_number="L9110 H-bridge"]
  Part2 = Arduino Uno (Rev3) - ICSP
  M1 = DC Motor
  M2 = DC Motor
  Part3 = Bluetooth HC-05 Macho
  VCC1 = Battery block 9V
  R1 = Resistor [tolerance=±5% resistance=1k package="1206 [SMD]"]
  R2 = Resistor [tolerance=±5% resistance=2k package="1206 [SMD]"]
  VCC2 = Battery block 9V
  JACK1 = 2.1mm Barrel Jack with Terminal Block
  Part5 = Arduino Nano (Rev3.0) (ICSP)
  Part6 = InvenSense MPU6050
  Part7 = Bluetooth HC-05 Macho
  R3 = Resistor [tolerance=±5% resistance=1k package="1206 [SMD]"]
  R4 = Resistor [tolerance=±5% resistance=2k package="1206 [SMD]"]

nets:
  N1: U1.B-IA, Part2.D10_PWM/SS
  N2: U1.B-IB, Part2.D9_PWM
  N3: U1.GND, VCC1.-
  N4: U1.VCC, VCC1.+
  N5: U1.A-IA, Part2.D6_PWM
  N6: U1.A-IB, Part2.D5_PWM
  N7: U1.MOTOR_A-A, M2.pin_2
  N8: U1.MOTOR_A-B, M2.pin_1
  N9: U1.MOTOR_B-A, M1.pin_2
  N10: U1.MOTOR_B-B, M1.pin_1
  GND: Part2.GND, Part3.GND
  N11: Part2.D2, Part3.TXD
  N12: Part2.D3_PWM, R1.Pin_0, R2.Pin_1
  5V: Part2.5V, Part3.VCC
  N13: Part3.RXD, R1.Pin_1
  N14: VCC2.-, JACK1.NEG
  N15: VCC2.+, JACK1.POS
  GND_2: Part5.GND, Part6.GND
  N16: Part5.D2, Part7.TXD
  N17: Part5.D3, R3.Pin_0
  5V_2: Part5.5V, Part6.VCC
  N18: Part5.A5, Part6.SCL
  N19: Part5.A4, Part6.SDA
  N20: Part7.RXD, R3.Pin_1, R4.Pin_0
  N21: Part7.GND, R4.Pin_1
