# Fritzing sketch HPV_Camera_Display (saved by Fritzing 0.9.3b)

parts:
  MH-ET_LIVE_ESP32_DEVKIT1 = MH-ET LIVE ESP32 DEVKIT 38 pins
  Part1 = TFT 2.8 inch 320x240 Touch w microSD [part_number=1770]
  Mod1 = ESP32 - CAM
  USBTTL1 = USB TTL Serial Cable

nets:
  N1: MH-ET_LIVE_ESP32_DEVKIT1.3V3, Part1.LCD_LITE
  5V: MH-ET_LIVE_ESP32_DEVKIT1.5V, Part1.+5V
  GND: MH-ET_LIVE_ESP32_DEVKIT1.GND, Part1.GND
  N2: MH-ET_LIVE_ESP32_DEVKIT1.IO23, Part1.MOSI
  N3: MH-ET_LIVE_ESP32_DEVKIT1.IO19, Part1.MISO
  N4: MH-ET_LIVE_ESP32_DEVKIT1.IO18, Part1.SCLK
  N5: MH-ET_LIVE_ESP32_DEVKIT1.IO4, Part1.LCD_RST
  N6: MH-ET_LIVE_ESP32_DEVKIT1.IO2, Part1.LCD_DC
  N7: MH-ET_LIVE_ESP32_DEVKIT1.IO15, Part1.LCD_CS
  5V_2: Mod1.5V, USBTTL1.5V
  GND_2: Mod1.GND, USBTTL1.GND
  N8: Mod1.VOT, USBTTL1.RX
  N9: Mod1.VOR, USBTTL1.TX

custom parts:
  MH-ET LIVE ESP32 DEVKIT 38 pins: http://mh.nodebb.com/topic/2/mh-et-live-esp32-devkit
  TFT 2.8 inch 320x240 Touch w microSD: This TFT display is big (2.8" diagonal) bright (4 white-LED backlight) and colorful! 240x320 pixels with individual RGB pixel control. As a bonus, this display has a resistive touchscreen attached to it already, so you can detect finger presses anywhere on the screen.
  ESP32 - CAM: The ESP32-CAM has a very competitive small-size camera module that can operate independently as a minimum system with a footprint of only 27*40.5*4.5mm and a deep sleep current of up to 6mA.
